# Fritzing sketch Alraune (saved by Fritzing 0.9.10b)
perfboards: 1

parts:
  SPKR1 = Loudspeaker
  WeMos_D1_Mini1 = WeMos D1 Mini
  DFRobot_DFPlayer_Mini1 = DFRobot DFPlayer Mini [part_number=DFR0299]
  M1 = DC Motor [voltage_(max)=6V voltage_(min)=3V]
  Bauteil1 = Soil Moisture Sensor
  KY-1 = Keyes Relay [package=THT]

nets:
  N1: SPKR1.pin1, DFRobot_DFPlayer_Mini1.SPK_2
  N2: SPKR1.pin2, DFRobot_DFPlayer_Mini1.SPK_1
  3V3: WeMos_D1_Mini1.3V3, Bauteil1.VCC
  5V: WeMos_D1_Mini1.5V, DFRobot_DFPlayer_Mini1.VCC, KY-1.signal, KY-1.NO
  N3: WeMos_D1_Mini1.A0, Bauteil1.SIG
  N4: WeMos_D1_Mini1.D0, KY-1.ground
  N5: WeMos_D1_Mini1.D3, DFRobot_DFPlayer_Mini1.RX
  N6: WeMos_D1_Mini1.D4, DFRobot_DFPlayer_Mini1.TX
  N7: WeMos_D1_Mini1.G, DFRobot_DFPlayer_Mini1.GND-1, DFRobot_DFPlayer_Mini1.GND-2, Bauteil1.GND, KY-1.power
  N8: M1.pin_2, KY-1.C

custom parts:
  Keyes Relay: The Keyes 5V relay module is suitable for SCM development, home appliance control. It uses a 5V~12V TIL control signal which can control DC / AC signal.
