# Fritzing sketch Audioplayer (saved by Fritzing 0.9.10b)
perfboards: 1

parts:
  SPKR1 = Loudspeaker
  WeMos_D1_Mini1 = WeMos D1 Mini
  DFRobot_DFPlayer_Mini1 = DFRobot DFPlayer Mini [part_number=DFR0299]

nets:
  N1: SPKR1.pin1, DFRobot_DFPlayer_Mini1.SPK_2
  N2: SPKR1.pin2, DFRobot_DFPlayer_Mini1.SPK_1
  5V: WeMos_D1_Mini1.5V, DFRobot_DFPlayer_Mini1.VCC
  N3: WeMos_D1_Mini1.D3, DFRobot_DFPlayer_Mini1.RX
  N4: WeMos_D1_Mini1.D4, DFRobot_DFPlayer_Mini1.TX
  N5: WeMos_D1_Mini1.G, DFRobot_DFPlayer_Mini1.GND-1, DFRobot_DFPlayer_Mini1.GND-2
