# Fritzing sketch Feuchtigkeitssensor (saved by Fritzing 0.9.10b)
perfboards: 1

parts:
  WeMos_D1_Mini1 = WeMos D1 Mini
  Bauteil1 = Soil Moisture Sensor

nets:
  3V3: WeMos_D1_Mini1.3V3, Bauteil1.VCC
  N1: WeMos_D1_Mini1.A0, Bauteil1.SIG
  N2: WeMos_D1_Mini1.G, Bauteil1.GND
