# Fritzing sketch Pumpe (saved by Fritzing 0.9.10b)
perfboards: 1

parts:
  WeMos_D1_Mini1 = WeMos D1 Mini
  M1 = DC Motor [voltage_(max)=6V voltage_(min)=3V]
  KY-1 = Keyes Relay [package=THT]

nets:
  N1: WeMos_D1_Mini1.5V, KY-1.signal, KY-1.NO
  N2: WeMos_D1_Mini1.D0, KY-1.ground
  N3: WeMos_D1_Mini1.G, KY-1.power
  N4: M1.pin_2, KY-1.C

custom parts:
  Keyes Relay: The Keyes 5V relay module is suitable for SCM development, home appliance control. It uses a 5V~12V TIL control signal which can control DC / AC signal.
